# Fritzing sketch Final schematic iot (saved by Fritzing 0.9.3b)

parts:
  Mod1 = ESP32 - CAM
  PIR1 = PIR sensor
  FTDI1 = FTDI Friend
  Mod2 = ESP32 - CAM
  PIR2 = PIR sensor
  Mod3 = ESP32 - CAM
  Q2 = npn-Powertransistor [package="TO220 [THT]"]
  IC2 = Voltage Regulator [package=to220-igo]  # not connected
  S1 = Round Pushbutton
  D2 = Schottky Diode [part_number=1N5817 package="Melf DO-213 AB [SMD]"]
  C1 = Capacitor Polarized [package=panasonic_c]
  BAT1 = BC9VPC [package=bc9vpc]
  R5 = Resistor [tolerance=±5% resistance=220 package="2010 [SMD]"]
  R6 = Resistor [tolerance=±5% resistance=220 package="2010 [SMD]"]
  R7 = Resistor [tolerance=±5% resistance=220 package="2010 [SMD]"]

nets:
  5V: Mod1.5V, PIR1.VDD
  GND: Mod1.GND, PIR1.GND
  N1: Mod1.IO13, PIR1.SIG
  GND_2: FTDI1.GND, Mod2.GND, Mod2.IO0, PIR2.GND
  VCC: FTDI1.VCC, Mod2.3V3
  N2: FTDI1.TX, Mod2.VOR
  N3: FTDI1.RX, Mod2.VOT
  5V_2: Mod2.5V, PIR2.VDD
  N4: Mod2.IO13, PIR2.SIG
  N5: Mod3.5V, C1.+
  N6: Mod3.GND, C1.-
  N7: Mod3.IO12, R5.Pin_0, R6.Pin_1
  N8: Mod3.IO13, S1.leg0, R7.Pin_1
  N9: Q2.base, R5.Pin_1
  N10: Q2.collector, D2.cathode
  N11: Q2.emitter, BAT1.V-
  N12: D2.anode, BAT1.V+

custom parts:
  ESP32 - CAM: The ESP32-CAM has a very competitive small-size camera module that can operate independently as a minimum system with a footprint of only 27*40.5*4.5mm and a deep sleep current of up to 6mA.
